// Logisim project lab4a.circ as structural Verilog: 8 circuits, main circuit main
module main (
  input  WL_1,
  input  WL_2,
  input  WL_3,
  input  WL_4
);

  wire s0_out_5, S1_out_5, S2_out_5, S3_out_5, s4_out_5, s5_out_5, s6_out_5;

  S0 s0 (.in_1(WL_1), .in_2(WL_2), .in_3(WL_3), .in_4(WL_4), .out_5(s0_out_5));
  S1 S1 (.in_1(WL_1), .in_2(WL_2), .in_3(WL_3), .in_4(WL_4), .out_5(S1_out_5));
  S2 S2 (.in_1(WL_1), .in_2(WL_2), .in_3(WL_3), .in_4(WL_4), .out_5(S2_out_5));
  S3 S3 (.in_1(WL_1), .in_2(WL_2), .in_3(WL_3), .in_4(WL_4), .out_5(S3_out_5));
  S4 s4 (.in_1(WL_1), .in_2(WL_2), .in_3(WL_3), .in_4(WL_4), .out_5(s4_out_5));
  S5 s5 (.in_1(WL_1), .in_2(WL_2), .in_3(WL_3), .in_4(WL_4), .out_5(s5_out_5));
  S6 s6 (.in_1(WL_1), .in_2(WL_2), .in_3(WL_3), .in_4(WL_4), .out_5(s6_out_5));
  _7_Segment_Display u_7_segment_display_1 (
    .g(s0_out_5), .f(S1_out_5), .a(S2_out_5), .b(S3_out_5), .e(s4_out_5), .d(s5_out_5), .c(s6_out_5));  // open: dp
endmodule

module S0 (
  input  in_1,
  input  in_2,
  input  in_3,
  input  in_4,
  output out_5
);

  wire or_1_out, or_2_out;

  or or_1 (or_1_out, in_1, in_2, in_3, in_4);
  or or_2 (or_2_out, ~in_1, in_2, in_3, in_4);  // OR_Gate
  and and_1 (out_5, or_1_out, or_2_out);
endmodule

module S1 (
  input  in_1,
  input  in_2,
  input  in_3,
  input  in_4,
  output out_5
);

  wire or_1_out, or_2_out, or_3_out;

  or or_1 (or_1_out, ~in_1, in_2, in_3, in_4);  // OR_Gate
  or or_2 (or_2_out, ~in_1, ~in_2, in_3, in_4);  // OR_Gate
  or or_3 (or_3_out, ~in_1, ~in_2, ~in_3, in_4);  // OR_Gate
  and and_1 (out_5, or_1_out, or_2_out, or_3_out);
endmodule

module S2 (
  input  in_1,
  input  in_2,
  input  in_3,
  input  in_4,
  output out_5
);

  wire or_1_out, or_2_out;

  or or_1 (or_1_out, ~in_1, in_2, in_3, in_4);  // OR_Gate
  or or_2 (or_2_out, ~in_1, ~in_2, ~in_3, ~in_4);  // OR_Gate
  and and_1 (out_5, or_1_out, or_2_out);
endmodule

module S3 (
  input  in_1,
  input  in_2,
  input  in_3,
  input  in_4,
  output out_5
);

  wire and_1_out, and_2_out, and_3_out, and_4_out, and_5_out;

  and and_1 (and_1_out, ~in_1, ~in_2, ~in_3, ~in_4);  // AND_Gate
  and and_2 (and_2_out, in_1, ~in_2, ~in_3, ~in_4);  // AND_Gate
  and and_3 (and_3_out, in_1, in_2, ~in_3, ~in_4);  // AND_Gate
  and and_4 (and_4_out, in_1, in_2, in_3, ~in_4);  // AND_Gate
  and and_5 (and_5_out, in_1, in_2, in_3, in_4);
  or or_1 (out_5, and_1_out, and_2_out, and_3_out, and_4_out, and_5_out);
endmodule

module S4 (
  input  in_1,
  input  in_2,
  input  in_3,
  input  in_4,
  output out_5
);

  wire or_1_out, or_2_out, or_3_out;

  or or_1 (or_1_out, ~in_1, in_2, in_3, in_4);  // OR_Gate
  or or_2 (or_2_out, ~in_1, ~in_2, ~in_3, in_4);  // OR_Gate
  or or_3 (or_3_out, ~in_1, ~in_2, ~in_3, ~in_4);  // OR_Gate
  and and_1 (out_5, or_1_out, or_2_out, or_3_out);
endmodule

module S5 (
  input  in_1,
  input  in_2,
  input  in_3,
  input  in_4,
  output out_5
);

  wire or_1_out, or_2_out;

  or or_1 (or_1_out, ~in_1, in_2, in_3, in_4);  // OR_Gate
  or or_2 (or_2_out, ~in_1, ~in_2, ~in_3, ~in_4);  // OR_Gate
  and and_1 (out_5, or_1_out, or_2_out);
endmodule

module S6 (
  input  in_1,
  input  in_2,
  input  in_3,
  input  in_4,
  output out_5
);

  wire and_1_out, and_2_out, and_3_out, and_4_out;

  and and_1 (and_1_out, ~in_1, ~in_2, ~in_3, ~in_4);  // AND_Gate
  and and_2 (and_2_out, in_1, ~in_2, ~in_3, ~in_4);  // AND_Gate
  and and_3 (and_3_out, in_1, in_2, in_3, ~in_4);  // AND_Gate
  and and_4 (and_4_out, in_1, in_2, in_3, in_4);
  or or_1 (out_5, and_1_out, and_2_out, and_3_out, and_4_out);
endmodule
