// Logisim project lab11.circ as structural Verilog: 2 circuits, main circuit main
module main (
  input  GO,
  input  ESTOP,
  input  TOP,
  input  DIRECTION,
  input  BOTTOM,
  output MOTOR_UP,
  output MOTOR_DOWN
);

  NCTL nctl_1 (
    .GO(GO), .ESTOP(ESTOP), .TOP(TOP), .DIRECTION(DIRECTION), .BOTTOM(BOTTOM), .MOTOR_UP(MOTOR_UP),
    .MOTOR_DOWN(MOTOR_DOWN));
endmodule

module NCTL (
  input  GO,
  input  ESTOP,
  input  TOP,
  input  DIRECTION,
  input  BOTTOM,
  output MOTOR_UP,
  output MOTOR_DOWN
);

  wire and_1_out, and_2_out, and_3_out, not_1_out, or_1_out;

  or or_1 (or_1_out, and_1_out, GO);
  not not_1 (not_1_out, ESTOP);
  and and_1 (and_1_out, or_1_out, not_1_out);
  and and_2 (and_2_out, and_1_out, ~DIRECTION);  // AND_Gate
  and and_3 (and_3_out, DIRECTION, and_1_out);
  and and_4 (MOTOR_UP, ~TOP, and_2_out);  // AND_Gate
  and and_5 (MOTOR_DOWN, and_3_out, ~BOTTOM);  // AND_Gate
endmodule
